// Logisim project TotalALU.circ as structural Verilog: 1 circuit, main circuit main
module main (
  input  oc1,
  input  oc2,
  input  oc3,
  input  oc4,
  input  Cin,
  input  A1,
  input  A2,
  input  A3,
  input  A4,
  input  A5,
  input  A6,
  input  A7,
  input  A8,
  input  B1,
  input  B2,
  input  B3,
  input  B4,
  input  B5,
  input  B6,
  input  B7,
  input  B8,
  output o1,
  output o2,
  output o3,
  output o4,
  output o5,
  output o6,
  output o7,
  output o8,
  output C,
  output N,
  output Z,
  output V
);

  wire ADC_out, ADD_out, and_1_out, and_2_out, and_3_out, and_4_out, and_5_out, and_6_out, and_7_out,
       and_8_out, and_9_out, and_10_out, and_11_out, and_12_out, and_13_out, and_14_out, and_15_out,
       and_16_out, and_17_out, and_18_out, and_19_out, and_20_out, and_21_out, and_22_out, and_23_out,
       and_24_out, and_25_out, and_26_out, and_27_out, and_28_out, and_29_out, and_30_out, and_31_out,
       and_32_out, and_33_out, and_34_out, and_35_out, and_36_out, and_37_out, and_38_out, and_39_out,
       and_40_out, and_41_out, and_42_out, and_43_out, and_44_out, and_45_out, and_46_out, and_47_out,
       and_48_out, and_49_out, and_50_out, and_51_out, and_52_out, and_53_out, and_54_out, and_55_out,
       and_56_out, and_57_out, ANDu_out, ASR_out, CE_out, EA_out, HC_out, IB_out, LC_out, LS_out, LSL_out,
       LSR_out, nand_1_out, nand_2_out, nand_3_out, nand_4_out, nand_5_out, nand_6_out, nand_7_out,
       nand_8_out, nor_1_out, nor_2_out, nor_3_out, nor_4_out, nor_5_out, nor_6_out, nor_7_out, nor_8_out,
       nor_9_out, nor_10_out, nor_11_out, nor_12_out, nor_13_out, nor_14_out, nor_15_out, nor_16_out,
       nor_17_out, nor_18_out, nor_19_out, nor_20_out, nor_21_out, nor_22_out, nor_23_out, nor_24_out,
       nor_25_out, nor_26_out, nor_27_out, nor_28_out, nor_29_out, nor_30_out, nor_31_out, nor_32_out,
       nor_33_out, nor_34_out, nor_35_out, nor_36_out, nor_37_out, nor_38_out, nor_39_out, nor_40_out,
       nor_41_out, not_1_out, not_2_out, not_3_out, not_4_out, ONC_out, or_1_out, or_2_out, or_3_out,
       or_4_out, or_5_out, or_6_out, or_7_out, ORu_out, RC_out, RCL_out, RCR_out, ROLu_out, RORu_out, RS_out,
       SBB_out, SUB_out, TWC_out, X1_out, x2_out, x3_out, xnor_2_out, XORu_out;

  not not_1 (not_1_out, oc1);
  not not_2 (not_2_out, oc2);
  not not_3 (not_3_out, oc3);
  not not_4 (not_4_out, oc4);
  and and_1 (and_1_out, Cin, CE_out);
  and and_2 (and_2_out, B8, LC_out);
  nand ADD (ADD_out, not_4_out, not_3_out, not_2_out, not_1_out);
  nand CE (CE_out, RCR_out, RCL_out, ADC_out, SBB_out);
  and and_3 (and_3_out, B1, RC_out);
  or or_1 (or_1_out, and_1_out, and_2_out, and_3_out, HC_out);
  nand nand_1 (nand_1_out, EA_out, A1);
  nor nor_1 (nor_1_out, IB_out, B1);
  nand nand_2 (nand_2_out, EA_out, A2);
  nor nor_2 (nor_2_out, IB_out, B2);
  nand nand_3 (nand_3_out, EA_out, A3);
  nor nor_3 (nor_3_out, IB_out, B3);
  nand nand_4 (nand_4_out, EA_out, A4);
  nor nor_4 (nor_4_out, IB_out, B4);
  nand nand_5 (nand_5_out, EA_out, A5);
  nor nor_5 (nor_5_out, IB_out, B5);
  nand nand_6 (nand_6_out, EA_out, A6);
  nor nor_6 (nor_6_out, IB_out, B6);
  nand nand_7 (nand_7_out, EA_out, A7);
  nor nor_7 (nor_7_out, IB_out, B7);
  nand nand_8 (nand_8_out, EA_out, A8);
  nor nor_8 (nor_8_out, IB_out, B8);
  nand ADC (ADC_out, not_4_out, not_3_out, not_2_out, oc1);
  nand LC (LC_out, RORu_out, ASR_out);
  nand SUB (SUB_out, not_4_out, not_3_out, not_1_out, oc2);
  not RC (RC_out, ROLu_out);
  and and_4 (and_4_out, nand_1_out, X1_out, nor_1_out);
  nor nor_9 (nor_9_out, nand_1_out, x2_out, nor_1_out);
  and and_5 (and_5_out, nand_2_out, X1_out, nor_2_out);
  nor nor_10 (nor_10_out, nand_2_out, x2_out, nor_2_out);
  and and_6 (and_6_out, nand_3_out, X1_out, nor_3_out);
  nor nor_11 (nor_11_out, nand_3_out, x2_out, nor_3_out);
  and and_7 (and_7_out, nand_4_out, X1_out, nor_4_out);
  nor nor_12 (nor_12_out, nand_4_out, x2_out, nor_4_out);
  and and_8 (and_8_out, nand_5_out, X1_out, nor_5_out);
  nor nor_13 (nor_13_out, nand_5_out, X1_out, nor_5_out);
  and and_9 (and_9_out, nand_6_out, X1_out, nor_6_out);
  nor nor_14 (nor_14_out, nand_6_out, x2_out, nor_6_out);
  and and_10 (and_10_out, nand_7_out, X1_out, nor_7_out);
  nor nor_15 (nor_15_out, nand_7_out, x2_out, nor_7_out);
  and and_11 (and_11_out, nand_8_out, X1_out, nor_8_out);
  nor nor_16 (nor_16_out, nand_8_out, x2_out, nor_8_out);
  nand SBB (SBB_out, not_4_out, not_3_out, oc2, oc1);
  nand HC (HC_out, SUB_out, TWC_out, ANDu_out, XORu_out);
  nor nor_17 (nor_17_out, and_4_out, nor_9_out);
  nor nor_18 (nor_18_out, and_5_out, nor_10_out);
  nor nor_19 (nor_19_out, and_6_out, nor_11_out);
  nor nor_20 (nor_20_out, and_7_out, nor_12_out);
  nor nor_21 (nor_21_out, and_8_out, nor_13_out);
  nor nor_22 (nor_22_out, and_9_out, nor_14_out);
  nor nor_23 (nor_23_out, and_10_out, nor_15_out);
  nor nor_24 (nor_24_out, and_11_out, nor_16_out);
  nand ONC (ONC_out, not_4_out, not_2_out, not_1_out, oc3);
  and and_12 (and_12_out, or_1_out, nor_17_out);
  nor nor_25 (nor_25_out, or_1_out, nor_17_out);
  and and_13 (and_13_out, or_2_out, nor_18_out);
  nor nor_26 (nor_26_out, or_2_out, nor_18_out);
  and and_14 (and_14_out, or_3_out, nor_19_out);
  nor nor_27 (nor_27_out, or_3_out, nor_19_out);
  and and_15 (and_15_out, or_4_out, nor_20_out);
  nor nor_28 (nor_28_out, or_4_out, nor_20_out);
  and and_16 (and_16_out, nor_22_out, nor_21_out);
  nor nor_29 (nor_29_out, nor_22_out, nor_21_out);
  and and_17 (and_17_out, or_5_out, nor_22_out);
  nor nor_30 (nor_30_out, or_5_out, nor_22_out);
  and and_18 (and_18_out, or_6_out, nor_23_out);
  nor nor_31 (nor_31_out, or_6_out, nor_23_out);
  and and_19 (and_19_out, or_7_out, nor_24_out);
  nor nor_32 (nor_32_out, or_7_out, nor_24_out);
  nand TWC (TWC_out, not_4_out, not_2_out, oc3, oc1);
  nand EA (EA_out, ADD_out, ADC_out, SUB_out, SBB_out, TWC_out, ORu_out, XORu_out);
  nand ANDu (ANDu_out, not_4_out, not_1_out, oc3, oc2);
  nand ORu (ORu_out, not_4_out, oc3, oc2, oc1);
  nand IB (IB_out, SUB_out, SBB_out, ONC_out, TWC_out, XORu_out);
  nand XORu (XORu_out, not_3_out, not_2_out, not_1_out, oc4);
  and and_20 (and_20_out, or_1_out, nor_17_out);
  and and_21 (and_21_out, or_1_out, nor_17_out, nor_18_out);
  and and_22 (and_22_out, nor_9_out, nor_18_out);
  and and_23 (and_23_out, or_1_out, nor_17_out, nor_18_out, nor_19_out);
  and and_24 (and_24_out, nor_9_out, nor_18_out, nor_19_out);
  and and_25 (and_25_out, nor_10_out, nor_19_out);
  and and_26 (and_26_out, or_1_out, nor_17_out, nor_18_out, nor_19_out, nor_20_out);
  and and_27 (and_27_out, nor_9_out, nor_18_out, nor_19_out, nor_20_out);
  and and_28 (and_28_out, nor_10_out, nor_19_out, nor_20_out);
  and and_29 (and_29_out, nor_11_out, nor_20_out);
  and and_30 (and_30_out, nor_22_out, nor_21_out);
  and and_31 (and_31_out, nor_22_out, nor_21_out);
  and and_32 (and_32_out, nor_13_out, nor_22_out);
  and and_33 (and_33_out, nor_22_out, nor_21_out, nor_22_out, nor_23_out);
  and and_34 (and_34_out, nor_13_out, nor_22_out, nor_23_out);
  and and_35 (and_35_out, nor_14_out, nor_23_out);
  and and_36 (and_36_out, nor_22_out, nor_21_out, nor_22_out, nor_23_out, nor_24_out);
  and and_37 (and_37_out, nor_13_out, nor_22_out, nor_23_out, nor_24_out);
  and and_38 (and_38_out, nor_14_out, nor_23_out, nor_24_out);
  and and_39 (and_39_out, nor_15_out, nor_24_out);
  nand LSL (LSL_out, not_3_out, not_2_out, oc4, oc1);
  nand X1 (X1_out, ADD_out, ADC_out, SUB_out, SBB_out, ONC_out, TWC_out, XORu_out, ORu_out);
  nand LSR (LSR_out, not_3_out, not_1_out, oc4, oc2);
  not x2 (x2_out, ORu_out);
  or or_2 (or_2_out, x3_out, and_20_out, nor_9_out);
  or or_3 (or_3_out, x3_out, and_21_out, and_22_out, nor_10_out);
  or or_4 (or_4_out, x3_out, and_23_out, and_24_out, and_25_out, nor_11_out);
  NotExactlyOne xnor_1 (
    .out(nor_22_out), .in0(x3_out), .in1(and_26_out), .in2(and_27_out), .in3(and_28_out), .in4(and_29_out),
    .in5(nor_12_out));
  or or_5 (or_5_out, x3_out, and_30_out, nor_13_out);
  or or_6 (or_6_out, x3_out, and_31_out, and_32_out, nor_14_out);
  or or_7 (or_7_out, x3_out, and_33_out, and_34_out, and_35_out, nor_15_out);
  NotExactlyOne xnor_2 (
    .out(xnor_2_out), .in0(x3_out), .in1(and_36_out), .in2(and_37_out), .in3(and_38_out), .in4(and_39_out),
    .in5(nor_16_out));
  nand ASR (ASR_out, not_3_out, oc4, oc2, oc1);
  not x3 (x3_out, XORu_out);
  nand ROLu (ROLu_out, not_2_out, not_1_out, oc4, oc3);
  nand RORu (RORu_out, not_2_out, oc4, oc3, oc1);
  nand RS (RS_out, ASR_out, LSR_out, RCR_out, RORu_out);
  nand RCL (RCL_out, not_1_out, oc4, oc3, oc2);
  nor nor_33 (nor_33_out, and_12_out, nor_25_out, LS_out, RS_out);
  and and_40 (and_40_out, or_1_out, LS_out);
  and and_41 (and_41_out, B2, RS_out);
  nor nor_34 (nor_34_out, and_13_out, nor_26_out, LS_out, RS_out);
  and and_42 (and_42_out, B1, LS_out);
  and and_43 (and_43_out, B3, RS_out);
  nor nor_35 (nor_35_out, and_14_out, nor_27_out, LS_out, RS_out);
  and and_44 (and_44_out, B2, LS_out);
  and and_45 (and_45_out, B4, RS_out);
  nor nor_36 (nor_36_out, and_15_out, nor_28_out, LS_out, RS_out);
  and and_46 (and_46_out, B3, LS_out);
  and and_47 (and_47_out, B5, RS_out);
  nor nor_37 (nor_37_out, and_16_out, nor_29_out, LS_out, RS_out);
  and and_48 (and_48_out, B4, LS_out);
  and and_49 (and_49_out, B6, RS_out);
  nor nor_38 (nor_38_out, and_17_out, nor_30_out, LS_out, RS_out);
  and and_50 (and_50_out, B5, LS_out);
  and and_51 (and_51_out, B7, RS_out);
  nor nor_39 (nor_39_out, and_18_out, nor_31_out, LS_out, RS_out);
  and and_52 (and_52_out, B6, LS_out);
  and and_53 (and_53_out, B8, RS_out);
  nor nor_40 (nor_40_out, and_19_out, nor_32_out, LS_out, RS_out);
  and and_54 (and_54_out, B7, LS_out);
  and and_55 (and_55_out, or_1_out, RS_out);
  nor nor_41 (nor_41_out, xnor_2_out, LS_out, RS_out);
  and and_56 (and_56_out, LS_out, B8);
  and and_57 (and_57_out, RS_out, B1);
  xnor xnor_3 (V, xnor_2_out, or_7_out);
  nand RCR (RCR_out, oc4, oc3, oc2, oc1);
  nand LS (LS_out, LSL_out, ROLu_out, RCL_out);
  or or_8 (o1, nor_33_out, and_40_out, and_41_out);
  or or_9 (o2, nor_34_out, and_42_out, and_43_out);
  or or_10 (o3, nor_35_out, and_44_out, and_45_out);
  or or_11 (o4, nor_36_out, and_46_out, and_47_out);
  or or_12 (o5, nor_37_out, and_48_out, and_49_out);
  or or_13 (o6, nor_38_out, and_50_out, and_51_out);
  or or_14 (o7, nor_39_out, and_52_out, and_53_out);
  or or_15 (N, nor_40_out, and_54_out, and_55_out);
  or or_16 (C, nor_41_out, and_56_out, and_57_out);
  nor nor_42 (Z, N, o7, o6, o5, o4, o3, o2, o1);

  assign o8 = N;
endmodule
